// Logisim project coa_project.circ as structural Verilog: 1 circuit, main circuit project
module project (
  input  in_1,
  input  [7:0] in_2,
  input  in_3,
  input  in_4,
  input  in_5,
  input  in_6,
  input  in_7,
  input  in_8,
  input  [7:0] in_9,
  input  in_10,
  input  in_11,
  input  in_12,
  input  [2:0] in_13,
  input  in_14,
  input  [1:0] in_15,
  input  [2:0] in_16,
  input  [2:0] in_17,
  input  [7:0] in_18,
  input  in_19,
  input  [2:0] in_20
);

  wire and_1_out, and_2_out, and_3_out, and_4_out, and_5_out, and_6_out, and_7_out, and_8_out,
       decoder_1_out0, decoder_1_out1, decoder_1_out2, decoder_1_out3, decoder_1_out4, decoder_1_out5,
       decoder_1_out6, decoder_1_out7, not_1_out;
  wire [7:0] adder_1_out, adder_2_out, adder_3_out, and_9_out, demultiplexer_1_out0, demultiplexer_1_out1,
       multiplexer_1_out, multiplexer_2_out, multiplexer_3_out, multiplexer_4_out, multiplexer_5_out,
       multiplexer_6_out, multiplexer_7_out, or_1_out, ram_1_dout, register_1_q, register_2_q, register_3_q,
       register_4_q, register_5_q, register_6_q, register_7_q, register_8_q, register_9_q, register_10_q,
       register_11_q, register_12_q, register_14_q, register_15_q, register_16_q, RZ_q;

  Decoder #(.select(3)) decoder_1 (
    .out0(decoder_1_out0), .out1(decoder_1_out1), .out2(decoder_1_out2), .out3(decoder_1_out3),
    .out4(decoder_1_out4), .out5(decoder_1_out5), .out6(decoder_1_out6), .out7(decoder_1_out7), .sel(in_20));  // open: en
  and and_1 (and_1_out, in_12, decoder_1_out0);
  and and_2 (and_2_out, in_12, decoder_1_out1);
  and and_3 (and_3_out, in_12, decoder_1_out2);
  and and_4 (and_4_out, in_12, decoder_1_out3);
  and and_5 (and_5_out, in_12, decoder_1_out4);
  and and_6 (and_6_out, in_12, decoder_1_out5);
  and and_7 (and_7_out, in_12, decoder_1_out6);
  and and_8 (and_8_out, in_12, decoder_1_out7);
  Register register_1 (.D(adder_1_out), .en(1'b1), .clk(in_11), .Q(register_1_q), .clr(in_8));
  Register RZ (.D(in_2), .en(1'b1), .clk(in_4), .Q(RZ_q), .clr(in_5));
  Adder adder_1 (.a(register_1_q), .b(8'h1), .out(adder_1_out));  // open: cin, cout
  Register register_2 (.D(register_16_q), .en(and_1_out), .clk(in_11), .Q(register_2_q));  // open: clr
  Register register_3 (.D(register_16_q), .en(and_2_out), .clk(in_11), .Q(register_3_q));  // open: clr
  Register register_4 (.D(register_16_q), .en(and_3_out), .clk(in_11), .Q(register_4_q));  // open: clr
  Register register_5 (.D(register_16_q), .en(and_4_out), .clk(in_11), .Q(register_5_q));  // open: clr
  Register register_6 (.D(register_16_q), .en(and_5_out), .clk(in_11), .Q(register_6_q));  // open: clr
  Register register_7 (.D(register_16_q), .en(and_6_out), .clk(in_11), .Q(register_7_q));  // open: clr
  Register register_8 (.D(register_16_q), .en(and_7_out), .clk(in_11), .Q(register_8_q));  // open: clr
  Register register_9 (.D(register_16_q), .en(and_8_out), .clk(in_11), .Q(register_9_q));  // open: clr
  Multiplexer #(.width(8)) multiplexer_1 (.in0(RZ_q), .in1(register_1_q), .out(multiplexer_1_out), .sel(in_7));
  RAM ram_1 (.addr(multiplexer_1_out), .we(in_1), .oe(in_3), .clk(in_11), .din(multiplexer_2_out), .dout(ram_1_dout));
  Multiplexer #(.width(8)) multiplexer_2 (.in0(register_12_q), .in1(in_9), .out(multiplexer_2_out), .sel(in_10));
  Multiplexer #(.select(3), .width(8)) multiplexer_3 (
    .in0(register_2_q), .in1(register_3_q), .in2(register_4_q), .in3(register_5_q), .in4(register_6_q),
    .in5(register_7_q), .in6(register_8_q), .in7(register_9_q), .out(multiplexer_3_out), .sel(in_13));
  Multiplexer #(.select(3), .width(8)) multiplexer_4 (
    .in0(register_2_q), .in1(register_3_q), .in2(register_4_q), .in3(register_5_q), .in4(register_6_q),
    .in5(register_7_q), .in6(register_8_q), .in7(register_9_q), .out(multiplexer_4_out), .sel(in_17));
  Register register_10 (.D(multiplexer_3_out), .en(1'b1), .clk(in_11), .Q(register_10_q), .clr(in_14));
  Register register_11 (.D(multiplexer_5_out), .en(1'b1), .clk(in_11), .Q(register_11_q));  // open: clr
  Multiplexer #(.width(8)) multiplexer_5 (.in0(multiplexer_4_out), .in1(in_18), .out(multiplexer_5_out), .sel(in_19));
  Register register_12 (.D(register_15_q), .en(1'b1), .clk(in_11), .Q(register_12_q));  // open: clr
  Demultiplexer #(.width(8)) demultiplexer_1 (
    .out0(demultiplexer_1_out0), .out1(demultiplexer_1_out1), .in(ram_1_dout), .sel(in_6));
  Adder adder_2 (.a(register_10_q), .b(register_11_q), .out(adder_2_out));  // open: cin, cout
  Adder adder_3 (.a(register_10_q), .b(register_11_q), .out(adder_3_out));  // open: cin, cout
  assign and_9_out = register_10_q & register_11_q;  // AND_Gate and_9, 8 bits wide
  assign or_1_out = register_10_q | register_11_q;  // OR_Gate or_1, 8 bits wide
  not not_1 (not_1_out, in_6);
  Register register_13 (.D(demultiplexer_1_out0), .en(not_1_out), .clk(in_11));  // open: Q, clr
  Register register_14 (.D(demultiplexer_1_out1), .en(in_6), .clk(in_11), .Q(register_14_q));  // open: clr
  Multiplexer #(.select(3), .width(8)) multiplexer_6 (
    .in0(adder_2_out), .in1(adder_3_out), .in2(and_9_out), .in3(or_1_out), .out(multiplexer_6_out),
    .sel(in_16));  // open: in4, in5, in6, in7
  Register register_15 (.D(multiplexer_6_out), .en(1'b1), .clk(in_11), .Q(register_15_q));  // open: clr
  Multiplexer #(.select(2), .width(8)) multiplexer_7 (
    .in0(register_15_q), .in1(register_14_q), .out(multiplexer_7_out), .sel(in_15));  // open: in2, in3
  Register register_16 (.D(multiplexer_7_out), .en(1'b1), .clk(in_11), .Q(register_16_q));  // open: clr

  // Notes on the sheet:
  //   Mem_Write
  //   Mem_Read
endmodule
